# Fritzing sketch BTVN_Tuan4 (saved by Fritzing 0.9.5d)

parts:
  Part1 = Arduino Uno (Rev3)
  M1 = DC Motor  # not connected
  M2 = DC Motor  # not connected
  L298N1 = L298N DC motor driver
  J1 = 2.1mm Barrel Jack with Terminal Block

nets:
  N1: Part1.D8, L298N1.IN1
  N2: Part1.D9_PWM, L298N1.ENA
  N3: Part1.D4, L298N1.ENB
  N4: Part1.D5_PWM, L298N1.IN4
  N5: Part1.D6_PWM, L298N1.IN3
  N6: Part1.D7, L298N1.IN2
  N7: L298N1.12V, J1.POS
  N8: L298N1.GND, J1.NEG

notes:
  Họ và tên sinh viên: Nguyễn Hoàng Hải
  MSV:25112038

custom parts:
  L298N DC motor driver: 2x DC motor driver with 78M05 positive voltage regulator (7..35 V) L298N: max 46 V, 2 A Set 5 V Enable jumper to enable 5 V regultor (needed for the L298N) and +5 V output at screw terminal or supply external +5 V at screw terminal Set ENA and/or ENB to +5 V to enable motor permanently or supply ENA and/or ENB with PWM signal IN1 and IN2 set rotation directory for motor A (OUT1/OUT2) IN2 and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
